// Logisim project SanjeevPenupala_Lab1.circ as structural Verilog: 1 circuit, main circuit main
module main (
  input  Input,
  input  Input1,
  input  Input2,
  input  Input1_2,
  input  Input2_2,
  input  A,
  input  A_2,
  input  B,
  input  B_2,
  input  C,
  input  C_2,
  input  D,
  input  D_2,
  input  A_3,
  input  A_4,
  input  B_3,
  input  B_4,
  input  C_3,
  input  C_4,
  input  D_3,
  input  D_4
);

  wire and_1_out, and_2_out, and_3_out, and_4_out, and_5_out, and_6_out, and_7_out, and_8_out, nand_1_out,
       nor_1_out, not_1_out, not_2_out, not_3_out, or_1_out, or_2_out, or_3_out, xor_1_out;

  not not_1 (not_1_out, Input);
  and and_1 (and_1_out, Input1, Input2);
  or or_1 (or_1_out, Input1_2, Input2_2);
  and and_2 (and_2_out, A, B);
  and and_3 (and_3_out, C, D);
  nand nand_1 (nand_1_out, A_3, B_3);
  and and_4 (and_4_out, C_3, D_3);
  LED Output (.in(not_1_out));
  LED Output_2 (.in(and_1_out));
  LED Output_3 (.in(or_1_out));
  and and_5 (and_5_out, and_2_out, and_3_out);
  or or_2 (or_2_out, nand_1_out, and_4_out);
  LED Y0 (.in(and_5_out));
  LED Y2 (.in(or_2_out));
  and and_6 (and_6_out, A_2, B_2);
  and and_7 (and_7_out, C_2, D_2);
  xor xor_1 (xor_1_out, A_4, B_4);
  nor nor_1 (nor_1_out, C_4, D_4);
  not not_2 (not_2_out, and_6_out);
  not not_3 (not_3_out, and_7_out);
  LED Y1 (.in(or_3_out));
  or or_3 (or_3_out, not_2_out, not_3_out);
  LED Y3 (.in(and_8_out));
  and and_8 (and_8_out, xor_1_out, nor_1_out);
endmodule
