// Logisim project SanjeevPenupala_Lab2.circ as structural Verilog: 1 circuit, main circuit main
module main (
  input  in_1,
  input  in_2,
  input  in_3,
  input  in_4,
  input  A,
  input  A_2,
  input  A_3,
  input  B,
  input  B_2,
  input  B_3,
  input  C_in,
  input  C,
  input  C_2
);

  wire decoder_1_out0, decoder_1_out1, decoder_1_out2, decoder_1_out3, decoder_1_out4, decoder_1_out5,
       decoder_1_out6, decoder_1_out7, multiplexer_1_out, multiplexer_2_out, or_1_out, or_2_out;

  Multiplexer #(.select(3)) multiplexer_1 (
    .in0(in_1), .in1(in_2), .in2(in_1), .in3(in_1), .in4(in_2), .in5(in_2), .in6(in_1), .in7(in_1),
    .out(multiplexer_1_out), .sel({C, B_2, A_2}));  // open: en
  LED Y0 (.in(multiplexer_1_out));
  LED Y1 (.in(multiplexer_2_out));
  Multiplexer #(.select(3)) multiplexer_2 (
    .in0(in_3), .in1(in_4), .in2(in_4), .in3(in_4), .in4(in_3), .in5(in_3), .in6(in_4), .in7(in_4),
    .out(multiplexer_2_out), .sel({C_2, B_3, A_3}));  // open: en
  Decoder #(.select(3)) decoder_1 (
    .out0(decoder_1_out0), .out1(decoder_1_out1), .out2(decoder_1_out2), .out3(decoder_1_out3),
    .out4(decoder_1_out4), .out5(decoder_1_out5), .out6(decoder_1_out6), .out7(decoder_1_out7),
    .sel({C_in, B, A}));  // open: en
  or or_1 (or_1_out, decoder_1_out7, decoder_1_out4, decoder_1_out2, decoder_1_out1);
  LED Sum (.in(or_1_out));
  or or_2 (or_2_out, decoder_1_out7, decoder_1_out6, decoder_1_out5, decoder_1_out3);
  LED C_out (.in(or_2_out));

  // Notes on the sheet:
  //   No equation given on lab report
  //   Built full adder to show how a decoder would work
endmodule
