// Logisim project SanjeevPenupala_Lab3.circ as structural Verilog: 1 circuit, main circuit main
module main (
  input  Carry_in,
  input  A3,
  input  A2,
  input  A1,
  input  A0,
  input  B3,
  input  B2,
  input  B1,
  input  B0,
  input  Carry_in_2,
  input  A,
  input  B,
  input  A3_2,
  input  A2_2,
  input  A1_2,
  input  A0_2,
  input  B3_2,
  input  B2_2,
  input  B1_2,
  input  B0_2
);

  wire adder_1_cout, adder_1_out, adder_2_cout, adder_2_out, adder_3_cout, adder_3_out, adder_4_cout,
       adder_4_out, adder_5_cout, adder_5_out, adder_6_cout, adder_6_out, adder_7_cout, adder_7_out,
       adder_8_cout, adder_8_out, adder_9_cout, adder_9_out, adder_10_cout, adder_10_out, adder_11_cout,
       adder_11_out, adder_12_cout, adder_12_out, adder_13_out, and_1_out, and_2_out, or_1_out, xor_1_out,
       xor_2_out, xor_3_out, xor_4_out, xor_5_out;

  Adder #(.width(1)) adder_1 (.a(A), .b(B), .out(adder_1_out), .cin(Carry_in), .cout(adder_1_cout));
  LED Sum (.in(adder_1_out));
  LED Carry (.in(adder_1_cout));
  xor xor_1 (xor_1_out, 1'b1, B0_2);
  buf xor_2 (xor_2_out, 1'b1);  // XOR_Gate
  xor xor_3 (xor_3_out, 1'b1, B2_2);
  xor xor_4 (xor_4_out, 1'b1, B3_2);
  Adder #(.width(1)) adder_2 (.a(xor_1_out), .b(A0_2), .out(adder_2_out), .cin(1'b1), .cout(adder_2_cout));
  Adder #(.width(1)) adder_3 (.a(xor_2_out), .b(A1_2), .out(adder_3_out), .cin(adder_2_cout), .cout(adder_3_cout));
  Adder #(.width(1)) adder_4 (.a(xor_3_out), .b(A2_2), .out(adder_4_out), .cin(adder_3_cout), .cout(adder_4_cout));
  Adder #(.width(1)) adder_5 (.a(xor_4_out), .b(A3_2), .out(adder_5_out), .cin(adder_4_cout), .cout(adder_5_cout));
  LED Diff_0 (.in(adder_2_out));
  LED Diff_1 (.in(adder_3_out));
  LED Diff_2 (.in(adder_4_out));
  LED Diff_3 (.in(adder_5_out));
  xor xor_5 (xor_5_out, adder_4_cout, adder_5_cout);
  LED Overflow (.in(xor_5_out));
  Adder #(.width(1)) adder_6 (.a(B0), .b(A0), .out(adder_6_out), .cin(Carry_in_2), .cout(adder_6_cout));
  Adder #(.width(1)) adder_7 (.a(B1), .b(A1), .out(adder_7_out), .cin(adder_6_cout), .cout(adder_7_cout));
  Adder #(.width(1)) adder_8 (.a(B2), .b(A2), .out(adder_8_out), .cin(adder_7_cout), .cout(adder_8_cout));
  Adder #(.width(1)) adder_9 (.a(B3), .b(A3), .out(adder_9_out), .cin(adder_8_cout), .cout(adder_9_cout));
  and and_1 (and_1_out, adder_9_out, adder_8_out);
  and and_2 (and_2_out, adder_9_out, adder_7_out);
  or or_1 (or_1_out, and_1_out, adder_9_cout, and_2_out);
  Adder #(.width(1)) adder_10 (.a(adder_6_out), .b(1'b0), .out(adder_10_out), .cout(adder_10_cout));  // open: cin
  Adder #(.width(1)) adder_11 (
    .a(adder_7_out), .b(or_1_out), .out(adder_11_out), .cin(adder_10_cout), .cout(adder_11_cout));
  Adder #(.width(1)) adder_12 (
    .a(adder_8_out), .b(or_1_out), .out(adder_12_out), .cin(adder_11_cout), .cout(adder_12_cout));
  Adder #(.width(1)) adder_13 (.a(adder_9_out), .b(1'b0), .out(adder_13_out), .cin(adder_12_cout));  // open: cout
  LED Low_0 (.in(adder_10_out));
  LED Low_1 (.in(adder_11_out));
  LED Low_2 (.in(adder_12_out));
  LED Low_3 (.in(adder_13_out));
  LED High_0 (.in(or_1_out));

  // Notes on the sheet:
  //   Adder
  //   4-bit Subtractor
  //   BCD Adder
endmodule
