// Logisim project SanjeevPenupala_Lab4.circ as structural Verilog: 1 circuit, main circuit main
module main (
  input  J,
  input  D,
  input  K,
  input  Preset,
  input  Preset_2,
  input  enable,
  input  enable_2,
  input  Carry_In,
  input  D0,
  input  D1,
  input  B0,
  input  D2,
  input  B1,
  input  D3,
  input  B2,
  input  B3
);

  wire A0_q, A1_q, A2_q, A3_q, adder_1_cout, adder_1_out, adder_2_cout, adder_2_out, adder_3_cout,
       adder_3_out, adder_4_cout, adder_4_out, Bit_0_q, Bit_1_q, Bit_2_q, Bit_3_q, clear_2_out, clear_3_out,
       Clear_4_out, Clear_out, Clock_2_out, Clock_3_out, Clock_4_out, Clock_out, d_ff_1_q, d_ff_1_qn,
       j_k_ff_1_q, j_k_ff_1_qn, not_1_out, not_2_out;

  Button Clock (.out(Clock_out));
  Button Clear (.out(Clear_out));
  Button Clock_2 (.out(Clock_2_out));
  not not_1 (not_1_out, Preset);
  LED Q (.in(d_ff_1_q));
  D_Flip_Flop d_ff_1 (
    .clk(Clock_2_out), .D(D), .Q(d_ff_1_q), .Qn(d_ff_1_qn), .preset(not_1_out), .en(enable),
    .reset(clear_2_out));
  LED Q_prime (.in(d_ff_1_qn));
  Button clear_2 (.out(clear_2_out));
  D_Flip_Flop Bit_0 (.clk(Clock_out), .D(D0), .Q(Bit_0_q), .reset(Clear_out));  // open: Qn, preset, en
  D_Flip_Flop Bit_1 (.clk(Clock_out), .D(D1), .Q(Bit_1_q), .reset(Clear_out));  // open: Qn, preset, en
  D_Flip_Flop Bit_2 (.clk(Clock_out), .D(D2), .Q(Bit_2_q), .reset(Clear_out));  // open: Qn, preset, en
  D_Flip_Flop Bit_3 (.clk(Clock_out), .D(D3), .Q(Bit_3_q), .reset(Clear_out));  // open: Qn, preset, en
  LED led_1 (.in(Bit_0_q));
  LED led_2 (.in(Bit_1_q));
  LED led_3 (.in(Bit_2_q));
  LED led_4 (.in(Bit_3_q));
  Button Clock_3 (.out(Clock_3_out));
  not not_2 (not_2_out, Preset_2);
  J_K_Flip_Flop j_k_ff_1 (
    .J(J), .clk(Clock_3_out), .K(K), .Q(j_k_ff_1_q), .Qn(j_k_ff_1_qn), .preset(not_2_out), .en(enable_2),
    .reset(clear_3_out));
  LED Q_2 (.in(j_k_ff_1_q));
  LED Q_prime_2 (.in(j_k_ff_1_qn));
  Button clear_3 (.out(clear_3_out));
  Adder #(.width(1)) adder_1 (.a(A0_q), .b(B0), .out(adder_1_out), .cin(Carry_In), .cout(adder_1_cout));
  Adder #(.width(1)) adder_2 (.a(A1_q), .b(B1), .out(adder_2_out), .cin(adder_1_cout), .cout(adder_2_cout));
  Adder #(.width(1)) adder_3 (.a(A2_q), .b(B2), .out(adder_3_out), .cin(adder_2_cout), .cout(adder_3_cout));
  Adder #(.width(1)) adder_4 (.a(A3_q), .b(B3), .out(adder_4_out), .cin(adder_3_cout), .cout(adder_4_cout));
  LED led_5 (.in(adder_4_cout));
  Button Clock_4 (.out(Clock_4_out));
  LED led_6 (.in(A0_q));
  D_Flip_Flop A0 (.clk(Clock_4_out), .D(adder_1_out), .Q(A0_q), .reset(Clear_4_out));  // open: Qn, preset, en
  D_Flip_Flop A1 (.clk(Clock_4_out), .D(adder_2_out), .Q(A1_q), .reset(Clear_4_out));  // open: Qn, preset, en
  LED led_7 (.in(A1_q));
  D_Flip_Flop A2 (.clk(Clock_4_out), .D(adder_3_out), .Q(A2_q), .reset(Clear_4_out));  // open: Qn, preset, en
  LED led_8 (.in(A2_q));
  LED led_9 (.in(A3_q));
  D_Flip_Flop A3 (.clk(Clock_4_out), .D(adder_4_out), .Q(A3_q), .reset(Clear_4_out));  // open: Qn, preset, en
  Button Clear_4 (.out(Clear_4_out));

  // Notes on the sheet:
  //   Part 1: D Flip-Flop
  //   Part 3: 4-Bit Register
  //   Part 2: J/K Flip-Flop
  //   Part 4: Accumulator
endmodule
